// Logisim project MoveComputer.circ as structural Verilog: 11 circuits, main circuit main
module main (
  input  in_1
);

  wire and_1_out, and_2_out, button_1_out, button_2_out, clock_1_out, movecore_1_paused, or_1_out, pla_1_out,
       por_1_out, ReadEnable, WriteEnable;
  wire [7:0] Addsress, DataIn, movecore_1_pausecode;

  Button button_1 (.out(button_1_out));
  or or_1 (or_1_out, button_1_out, por_1_out);
  Button button_2 (.out(button_2_out));
  LED led_1 (.in(movecore_1_paused));
  POR por_1 (.out(por_1_out));
  Hex_Digit_Display hex_digit_display_1 (.value(movecore_1_pausecode[7:4]));  // open: dp
  Hex_Digit_Display hex_digit_display_2 (.value(movecore_1_pausecode[3:0]));  // open: dp
  MoveCore movecore_1 (
    .PauseCode(movecore_1_pausecode), .Paused(movecore_1_paused), .WriteEnable(WriteEnable), .DataIn(DataIn),
    .ReadEnable(ReadEnable), .Address(Addsress), .PauseEnable(in_1), .Resume(button_2_out), .Reset(or_1_out),
    .Enable(1'b1));  // open: DataOut
  PLA #(.in_width(8), .out_width(1), .\table ("00101000 1\nxx0xxxxx 0\nxxxx0xxx 0")) pla_1 (
    .in(Addsress), .out(pla_1_out));
  Clock clock_1 (.out(clock_1_out));
  TTY #(.rows(32)) tty_1 (.data(DataIn[6:0]), .clk(clock_1_out), .we(and_1_out), .clr(and_2_out));
  and and_1 (and_1_out, pla_1_out, WriteEnable);
  and and_2 (and_2_out, and_1_out, DataIn[7]);
endmodule

module ALU (
  input  OutputEnable,
  input  [7:0] A,
  input  [7:0] B,
  input  [7:0] E,
  input  [7:0] M,
  output [7:0] R
);

  wire nor_1_out, not_1_out;
  wire [2:0] bitfinder_1_index, bitfinder_2_index, bitfinder_3_index, bitfinder_4_index;
  wire [3:0] bitadder_1_out;
  wire [7:0] adder_1_cout, adder_1_out, and_1_out, comparator_1_gt, comparator_2_gt, divider_1_out,
       divider_1_rem, divider_2_out, divider_2_rem, multiplier_1_cout, multiplier_1_out, multiplier_2_cout,
       multiplier_2_out, not_2_out, or_1_out, shifter_1_out, shifter_2_out, shifter_3_out, shifter_4_out,
       shifter_5_out, subtractor_1_bout, subtractor_1_out, undriven, xor_1_out;
  wire [7:3] pull_resistor_3_node, pull_resistor_4_node, pull_resistor_6_node, undriven_2;
  wire [7:4] pull_resistor_7_node;

  not not_1 (not_1_out, OutputEnable);
  Random random_1 ();  // open: clk, next, out, clr
  Clock clock_1 ();  // open: out
  Adder adder_1 (.a(A), .b(B), .out(adder_1_out), .cin(E[0]), .cout(adder_1_cout[0]));
  Subtractor subtractor_1 (.a(A), .b(B), .out(subtractor_1_out), .bin(E[0]), .bout(subtractor_1_bout[0]));
  Multiplier multiplier_1 (.a(A), .b(B), .out(multiplier_1_out), .cin(E), .cout(multiplier_1_cout));
  Divider divider_1 (.a(A), .b(B), .out(divider_1_out), .upper(E), .rem(divider_1_rem));
  Multiplier #(.mode("twosComplement")) multiplier_2 (
    .a(A), .b(B), .out(multiplier_2_out), .cin(E), .cout(multiplier_2_cout));
  Divider #(.mode("twosComplement")) divider_2 (.a(A), .b(B), .out(divider_2_out), .upper(E), .rem(divider_2_rem));
  BitFinder bitfinder_1 (.in(A), .index(bitfinder_1_index));  // open: found
  BitFinder #(.\type ("high1")) bitfinder_2 (.in(A), .index(bitfinder_2_index));  // open: found
  BitFinder #(.\type ("low0")) bitfinder_3 (.in(A), .index(bitfinder_3_index));  // open: found
  BitFinder #(.\type ("high0")) bitfinder_4 (.in(A), .index(bitfinder_4_index));  // open: found
  Shifter #(.shift("rl")) shifter_1 (.in(A), .\dist (B[2:0]), .out(shifter_1_out));
  Shifter #(.shift("rr")) shifter_2 (.in(A), .\dist (B[2:0]), .out(shifter_2_out));
  Shifter shifter_3 (.in(A), .\dist (B[2:0]), .out(shifter_3_out));
  Shifter #(.shift("lr")) shifter_4 (.in(A), .\dist (B[2:0]), .out(shifter_4_out));
  Shifter #(.shift("ar")) shifter_5 (.in(A), .\dist (B[2:0]), .out(shifter_5_out));
  BitAdder bitadder_1 (.in0(A), .out(bitadder_1_out));
  Comparator #(.mode("unsigned")) comparator_1 (
    .a(A), .b(B), .gt(comparator_1_gt[0]), .eq(comparator_1_gt[1]), .lt(comparator_1_gt[2]));
  Comparator comparator_2 (.a(A), .b(B), .gt(comparator_2_gt[0]), .eq(comparator_2_gt[1]), .lt(comparator_2_gt[2]));
  assign and_1_out = A & B;  // AND_Gate and_1, 8 bits wide
  assign or_1_out = A | B;  // OR_Gate or_1, 8 bits wide
  assign xor_1_out = A ^ B;  // XOR_Gate xor_1, 8 bits wide
  assign not_2_out = ~A;  // NOT_Gate not_2, 8 bits wide
  nor nor_1 (nor_1_out, M[5], M[6], M[7], not_1_out);
  Pull_Resistor pull_resistor_1 (.node(adder_1_cout));
  Pull_Resistor pull_resistor_2 (.node(subtractor_1_bout));
  Multiplexer #(.select(5), .width(8)) multiplexer_1 (
    .in0(A), .in1(B), .in2(E), .in3(undriven), .in4(adder_1_out), .in5(adder_1_cout), .in6(subtractor_1_out),
    .in7(subtractor_1_bout), .in8(multiplier_1_out), .in9(multiplier_1_cout), .in10(divider_1_out),
    .in11(divider_1_rem), .in12(multiplier_2_out), .in13(multiplier_2_cout), .in14(divider_2_out),
    .in15(divider_2_rem), .in16({pull_resistor_3_node, bitfinder_1_index}),
    .in17({undriven_2, bitfinder_2_index}), .in18({pull_resistor_4_node, bitfinder_3_index}),
    .in19({pull_resistor_6_node, bitfinder_4_index}), .in20(shifter_1_out), .in21(shifter_2_out),
    .in22(shifter_3_out), .in23(shifter_4_out), .in24(shifter_5_out),
    .in25({pull_resistor_7_node, bitadder_1_out}), .in26(comparator_1_gt), .in27(comparator_2_gt),
    .in28(and_1_out), .in29(or_1_out), .in30(xor_1_out), .in31(not_2_out), .out(R), .sel(M[4:0]),
    .en(nor_1_out));
  Pull_Resistor pull_resistor_3 (.node({pull_resistor_3_node, bitfinder_1_index}));
  Pull_Resistor pull_resistor_4 (.node({pull_resistor_4_node, bitfinder_3_index}));
  Pull_Resistor pull_resistor_5 (.node({pull_resistor_4_node, bitfinder_3_index}));
  Pull_Resistor pull_resistor_6 (.node({pull_resistor_6_node, bitfinder_4_index}));
  Pull_Resistor pull_resistor_7 (.node({pull_resistor_7_node, bitadder_1_out}));
  Pull_Resistor pull_resistor_8 (.node(comparator_1_gt));
  Pull_Resistor pull_resistor_9 (.node(comparator_2_gt));
endmodule

module MoveCore (
  input  [7:0] DataOut,
  input  Enable,
  input  PauseEnable,
  input  Reset,
  input  Resume,
  output WriteEnable,
  output [7:0] DataIn,
  output ReadEnable,
  output [7:0] Address,
  output [7:0] PauseCode,
  output Paused
);

  wire and_1_out, and_2_out, and_3_out, and_4_out, and_5_out, and_7_out, and_8_out, and_9_out, and_10_out,
       and_11_out, and_12_out, and_13_out, and_14_out, and_15_out, bitfinder_1_found, button_1_out,
       button_2_out, clock_1_out, clock_2_out, clock_3_out, clock_4_out, clock_5_out, clock_6_out,
       clock_7_out, clock_8_out, clock_9_out, ConditionalLongJump_out, ConditionalRelativeJump_out,
       decoder_1_out0, decoder_1_out1, decoder_1_out2, decoder_1_out3, decoder_1_out4, decoder_1_out5,
       decoder_1_out6, decoder_1_out7, decoder_2_out0, decoder_2_out1, decoder_2_out2, decoder_2_out3,
       decoder_2_out4, decoder_2_out5, decoder_2_out6, decoder_2_out7, decoder_3_out0, decoder_3_out1,
       decoder_3_out2, decoder_4_out1, decoder_4_out3, IncrementPC, nor_1_out, not_1_out, or_1_out, or_2_out,
       or_3_out, or_4_out, or_5_out, or_6_out, or_7_out, or_8_out, or_9_out, pla_1_out, pla_2_out, pla_3_out,
       pla_4_out, register_4_q, Reset_t, s_r_ff_1_qn;
  wire [1:0] counter_2_q;
  wire [7:0] A_q, B_q, Buff_q, E_q, HighByte_q, LowByte_q, multiplexer_1_out, multiplexer_2_out,
       multiplexer_3_out, multiplexer_4_out, multiplexer_5_out, multiplexer_7_out, pull_resistor_1_node,
       ram_1_dout, register_1_q, register_2_q, RelativeJump_q, rom_1_data;
  wire [8:0] CarryBuff_q;
  wire [8:8] and_6_out;
  wire [31:0] adder_1_out, bit_extender_1_out, multiplexer_6_out, PC;

  Decoder #(.select(3)) decoder_1 (
    .out0(decoder_1_out0), .out1(decoder_1_out1), .out2(decoder_1_out2), .out3(decoder_1_out3),
    .out4(decoder_1_out4), .out5(decoder_1_out5), .out6(decoder_1_out6), .out7(decoder_1_out7),
    .sel(Address[2:0]), .en(and_1_out));
  PLA #(.in_width(5), .out_width(1), .\table ("xx0xx 0\n00100 1 # Selected")) pla_1 (
    .in(Address[7:3]), .out(pla_1_out));
  and and_1 (and_1_out, pla_1_out, WriteEnable);
  or or_1 (or_1_out, decoder_1_out0, decoder_2_out6);
  or or_2 (or_2_out, decoder_1_out1, decoder_2_out6);
  or or_3 (or_3_out, decoder_1_out2, decoder_2_out6);
  or or_4 (or_4_out, decoder_1_out3, decoder_2_out6);
  BitFinder bitfinder_1 (.in(DataIn), .found(bitfinder_1_found));  // open: index
  and ConditionalLongJump (ConditionalLongJump_out, bitfinder_1_found, decoder_1_out7);
  and ConditionalRelativeJump (ConditionalRelativeJump_out, bitfinder_1_found, decoder_1_out5);
  Multiplexer #(.enable("false"), .width(8)) multiplexer_1 (
    .in0(RelativeJump_q), .in1(DataIn), .out(multiplexer_1_out), .sel(decoder_1_out6));
  Register LowByte (.D(multiplexer_2_out), .en(or_1_out), .clk(clock_1_out), .Q(LowByte_q));  // open: clr
  Multiplexer #(.enable("false"), .width(8)) multiplexer_2 (
    .in0(PC[7:0]), .in1(DataIn), .out(multiplexer_2_out), .sel(decoder_1_out0));
  Register register_1 (.D(multiplexer_3_out), .en(or_2_out), .clk(clock_1_out), .Q(register_1_q));  // open: clr
  Multiplexer #(.enable("false"), .width(8)) multiplexer_3 (
    .in0(PC[15:8]), .in1(DataIn), .out(multiplexer_3_out), .sel(decoder_1_out1));
  Register register_2 (.D(multiplexer_4_out), .en(or_3_out), .clk(clock_1_out), .Q(register_2_q));  // open: clr
  Multiplexer #(.enable("false"), .width(8)) multiplexer_4 (
    .in0(PC[23:16]), .in1(DataIn), .out(multiplexer_4_out), .sel(decoder_1_out2));
  Register HighByte (.D(multiplexer_5_out), .en(or_4_out), .clk(clock_1_out), .Q(HighByte_q));  // open: clr
  Multiplexer #(.enable("false"), .width(8)) multiplexer_5 (
    .in0(PC[31:24]), .in1(DataIn), .out(multiplexer_5_out), .sel(decoder_1_out3));
  Register RelativeJump (.D(DataIn), .en(decoder_1_out4), .clk(clock_1_out), .Q(RelativeJump_q));  // open: clr
  Clock clock_1 (.out(clock_1_out));
  or or_5 (or_5_out, ConditionalLongJump_out, decoder_2_out7);
  or or_6 (or_6_out, or_5_out, decoder_1_out6, ConditionalRelativeJump_out);
  and and_2 (and_2_out, ~or_6_out, IncrementPC);  // AND_Gate
  Pull_Resistor pull_resistor_1 (.node(pull_resistor_1_node));
  assign bit_extender_1_out = {{24{multiplexer_1_out[7]}}, multiplexer_1_out};  // Bit_Extender bit_extender_1
  Multiplexer #(.enable("false"), .width(32)) multiplexer_6 (
    .in0(adder_1_out), .in1({HighByte_q, register_2_q, register_1_q, LowByte_q}), .out(multiplexer_6_out),
    .sel(or_5_out));
  Counter #(.max('hffffffff), .width(32)) counter_1 (
    .load(or_6_out), .D(multiplexer_6_out), .count(and_2_out), .Q(PC), .clk(clock_3_out), .clr(or_7_out));  // open: carry, up
  nor nor_1 (nor_1_out, Address[7], Address[6], Address[5]);
  Register #(.trigger("high"), .width(9)) CarryBuff (
    .D({and_6_out[8], pull_resistor_1_node}), .en(ReadEnable), .clk(clock_2_out), .Q(CarryBuff_q));  // open: clr
  Clock clock_2 (.out(clock_2_out));
  and and_3 (and_3_out, pla_1_out, ReadEnable);
  assign DataOut = decoder_2_out0 ? LowByte_q : 8'bz;  // Controlled_Buffer controlled_buffer_1
  assign DataOut = decoder_2_out1 ? register_1_q : 8'bz;  // Controlled_Buffer controlled_buffer_2
  assign DataOut = decoder_2_out2 ? register_2_q : 8'bz;  // Controlled_Buffer controlled_buffer_3
  assign DataOut = decoder_2_out3 ? HighByte_q : 8'bz;  // Controlled_Buffer controlled_buffer_4
  assign DataOut = decoder_2_out4 ? RelativeJump_q : 8'bz;  // Controlled_Buffer controlled_buffer_5
  Adder #(.width(32)) adder_1 (.a(bit_extender_1_out), .b(PC), .out(adder_1_out));  // open: cin, cout
  or or_7 (or_7_out, and_4_out, Reset_t);
  and and_4 (and_4_out, decoder_2_out5, clock_3_out);
  Pull_Resistor pull_resistor_2 (.node(Reset_t));
  and and_5 (and_5_out, nor_1_out, WriteEnable);
  and and_6 (and_6_out[8], nor_1_out, ReadEnable);
  and and_7 (and_7_out, WriteEnable, CarryBuff_q[8]);
  Decoder #(.select(3)) decoder_2 (
    .out0(decoder_2_out0), .out1(decoder_2_out1), .out2(decoder_2_out2), .out3(decoder_2_out3),
    .out4(decoder_2_out4), .out5(decoder_2_out5), .out6(decoder_2_out6), .out7(decoder_2_out7),
    .sel(Address[2:0]), .en(and_3_out));
  Clock clock_3 (.out(clock_3_out));
  Decoder #(.select(5)) decoder_3 (
    .out0(decoder_3_out0), .out1(decoder_3_out1), .out2(decoder_3_out2), .sel(Address[4:0]), .en(and_5_out));  // open: out3, out4, out5, out6, out7, out8, out9, out10, out11, out12, out13, out14, out15, out16, out17, out18, out19, out20, out21, out22, out23, out24, out25, out26, out27, out28, out29, out30, out31
  Clock clock_4 (.out(clock_4_out));
  Multiplexer #(.enable("false"), .width(8)) multiplexer_7 (
    .in0(CarryBuff_q[7:0]), .in1(DataIn), .out(multiplexer_7_out), .sel(decoder_3_out2));
  or or_8 (or_8_out, decoder_3_out2, and_7_out);
  and and_8 (and_8_out, Address[7], ReadEnable);
  Clock clock_5 (.out(clock_5_out));
  Register A (.D(DataIn), .en(decoder_3_out0), .clk(clock_4_out), .Q(A_q));  // open: clr
  Register B (.D(DataIn), .en(decoder_3_out1), .clk(clock_4_out), .Q(B_q));  // open: clr
  Register E (.D(multiplexer_7_out), .en(or_8_out), .clk(clock_4_out), .Q(E_q));  // open: clr
  and and_9 (and_9_out, Address[7], WriteEnable);
  // Probe on A_q
  // Probe on B_q
  // Probe on E_q
  RAM #(.addrWidth(7)) ram_1 (
    .addr(Address[6:0]), .we(and_9_out), .oe(and_8_out), .clk(clock_5_out), .din(DataIn), .dout(ram_1_dout));
  PLA #(.in_width(8), .out_width(1), .\table ("00110000 1 # Selected\nxxxxxxxx 0 # Nothing")) pla_2 (
    .in(Address), .out(pla_2_out));
  // Probe on PC
  ALU3 alu3_1 (
    .OutputEnable(and_6_out[8]), .A(A_q), .B(B_q), .E(E_q), .M(Address), .R(DataOut), .S(pull_resistor_1_node));  // open: Carry
  assign DataOut = and_8_out ? ram_1_dout : 8'bz;  // Controlled_Buffer controlled_buffer_6
  // Probe on ram_1_dout
  Register register_3 (.D(DataIn), .en(and_10_out), .clk(clock_6_out), .Q(PauseCode), .clr(Reset_t));
  and and_10 (and_10_out, pla_2_out, PauseEnable, WriteEnable);
  Clock clock_6 (.out(clock_6_out));
  S_R_Flip_Flop s_r_ff_1 (
    .S(and_10_out), .R(1'b0), .clk(clock_6_out), .Q(Paused), .reset(or_9_out), .Qn(s_r_ff_1_qn));  // open: preset
  or or_9 (or_9_out, Resume, button_1_out, Reset_t);
  Button button_1 (.out(button_1_out));
  ROM #(.addrWidth(16)) rom_1 (.addr(PC[15:0]), .data(rom_1_data));
  PLA #(.in_width(8), .out_width(1), .\table ("00101001 1\nxx0xxxxx 0\nxxxx0xxx 0\nxxxxxxx0 0")) pla_3 (
    .in(rom_1_data), .out(pla_3_out));
  Clock clock_7 (.out(clock_7_out));
  Pull_Resistor pull_resistor_3 (.node(DataOut));
  Button button_2 (.out(button_2_out));
  PLA #(.in_width(8), .out_width(1), .\table ("00101000 1\nxx0xxxxx 0\nxxxx0xxx 0")) pla_4 (
    .in(Address), .out(pla_4_out));
  Register #(.trigger("high"), .width(1)) register_4 (
    .D(and_11_out), .en(ReadEnable), .clk(clock_7_out), .Q(register_4_q), .clr(Reset_t));
  and and_11 (and_11_out, pla_3_out, ReadEnable);
  Register #(.trigger("high")) Buff (.D(DataOut), .en(ReadEnable), .clk(clock_7_out), .Q(Buff_q));  // open: clr
  or or_10 (Reset_t, Reset, button_2_out);
  Clock clock_8 (.out(clock_8_out));
  TTY tty_1 (.data(DataIn[6:0]), .clk(clock_8_out), .we(and_12_out), .clr(and_15_out));
  and and_12 (and_12_out, pla_4_out, WriteEnable);
  and and_13 (and_13_out, register_4_q, WriteEnable);
  and and_14 (and_14_out, Enable, s_r_ff_1_qn);
  Clock clock_9 (.out(clock_9_out));
  and and_15 (and_15_out, and_12_out, DataIn[7]);
  // Probe on Address
  Multiplexer #(.enable("false"), .width(8)) multiplexer_8 (
    .in0(rom_1_data), .in1(8'h1), .out(Address), .sel(and_13_out));
  // Probe on DataIn
  Multiplexer #(.enable("false"), .width(8)) multiplexer_9 (
    .in0(Buff_q), .in1(rom_1_data), .out(DataIn), .sel(and_13_out));
  Counter #(.max('h3), .width(2)) counter_2 (
    .count(and_14_out), .Q(counter_2_q), .clk(not_1_out), .clr(Reset_t));  // open: load, D, carry, up
  not not_1 (not_1_out, clock_9_out);
  or or_11 (IncrementPC, decoder_4_out1, decoder_4_out3);
  Decoder #(.select(2)) decoder_4 (
    .out0(ReadEnable), .out1(decoder_4_out1), .out2(WriteEnable), .out3(decoder_4_out3), .sel(counter_2_q),
    .en(and_14_out));

  // Other names for the same wires on the sheet: Addsress[7:0] = Address; ClockBuf = ReadEnable

  // Notes on the sheet:
  //   contents of rom_1 (hex, n*v repeats v):
  //   0 0 29 ff 1 28 29 43 1 28 29 6f 1 28 29 6c 1 28 29 6c 1 28 29 61 1 28 29 74 1 28 29 7a 1 28 29 20 1
  //   28 29 63 1 28 29 6f 1 28 29 6e 1 28 29 6a 1 28 29 65 1 28 29 63 1 28 29 74 1 28 29 75 1 28 29 72 1
  //   28 29 65 1 28 29 a 1 28 29 0 1 85 26 3 29 1 85 81 85 82 85 83 3 84 29 20 1 8a 85 90 85 91 85 92 85
  //   93 85 94 81 95 82 96 83 97 84 98 85 2 29 d0 1 24 29 20 1 99 8*0 29 1 98 0 16 98 97 0 16 97 96 0 16
  //   96 95 0 16 95 29 43 94 0 1b 94 93 0 1b 93 92 0 1b 92 91 0 1b 91 90 0 1b 90 99 0 7 0 0 99 0 25 85 2
  //   90 0 29 4 17 0 2 80 85 2 29 30 4 28 80 0 4 28 91 0 29 4 17 0 2 80 85 2 29 30 4 28 80 0 4 28 92 0 29
  //   4 17 0 2 80 85 2 29 30 4 28 80 0 4 28 93 0 29 4 17 0 2 80 85 2 29 30 4 28 80 0 4 28 94 0 29 4 17 0 2
  //   80 85 2 29 30 4 28 80 0 4 28 29 a 1 28 29 58 1 20 29 1 84 0 1e 0 19 1 83 0 19 0 4 1 82 0 19 0 4 1 81
  //   0 19 0 4 0 29 55 1 30 29 2 1 2 1a 27 29 62 1 20 29 12 1 24 29 1 84 0 1c 25 81 0 17 81 82 0 17 82 83
  //   0 17 83 84 0 17 84 27 3 81 90 82 91 83 92 84 93 29 1 1 2 84 0 93 1 4 84 83 0 92 1 4 83 82 0 91 1 4
  //   82 81 0 90 1 4 81 85 2 84 0 93 1 4 84 83 0 92 1 4 83 82 0 91 1 4 82 81 0 90 1 4 81 27 3
endmodule

module MemoryInterface (
);

  wire and_1_out, bitfinder_1_found, clock_1_out;
  wire [4:0] pla_1_out;
  wire [7:0] ObjectOffset_q, ObjectSizeMinus1_q, StepSizeMinusObjectSize_q;
  wire [31:0] adder_1_out, controlled_buffer_1_out, Pointer_q;

  Register StepSizeMinusObjectSize (.Q(StepSizeMinusObjectSize_q));  // open: D, en, clk, clr
  Register ObjectSizeMinus1 (.Q(ObjectSizeMinus1_q));  // open: D, en, clk, clr
  Clock clock_1 (.out(clock_1_out));
  Register #(.width(32)) Pointer (.D(adder_1_out), .en(pla_1_out[4]), .clk(clock_1_out), .Q(Pointer_q));  // open: clr
  assign controlled_buffer_1_out[7:0] = pla_1_out[1] ? StepSizeMinusObjectSize_q : 8'bz;  // Controlled_Buffer controlled_buffer_1
  Pull_Resistor pull_resistor_1 (.node(controlled_buffer_1_out));
  Counter ObjectOffset (
    .load(pla_1_out[3]), .D(ObjectSizeMinus1_q), .count(pla_1_out[2]), .Q(ObjectOffset_q), .up(1'b0),
    .clk(clock_1_out));  // open: carry, clr
  Adder #(.width(32)) adder_1 (
    .a(Pointer_q), .b(controlled_buffer_1_out), .out(adder_1_out), .cin(pla_1_out[0]));  // open: cout
  BitFinder bitfinder_1 (.in(ObjectOffset_q), .found(bitfinder_1_found));  // open: index
  PLA #(.in_width(1), .out_width(5), .\table ("0 11011 # Load object\n1 10101 # NextByte")) pla_1 (
    .in(bitfinder_1_found), .out(pla_1_out));
  // Probe on Pointer_q
  and and_1 (and_1_out, clock_1_out, pla_1_out[0]);
  // Digital_Oscilloscope digital_oscilloscope_1: pin names not known; wires that end beside it: clock_1_out, bitfinder_1_found, pla_1_out[1], and_1_out
endmodule

module ALU2 (
  input  OutputEnable,
  input  [7:0] A,
  input  [7:0] B,
  input  [7:0] E,
  input  [7:0] M,
  output [7:0] R,
  output [7:0] S
);

  wire bitfinder_1_found, nor_1_out, not_1_out;
  wire [2:0] bitfinder_2_index, bitfinder_3_index, bitfinder_4_index, bitfinder_5_index, negator_1_out,
       negator_2_out;
  wire [3:0] bitadder_1_out;
  wire [7:0] adder_1_cout, adder_1_out, and_1_out, bitfinder_2_found, bitfinder_3_found, bitfinder_4_found,
       bitfinder_5_found, comparator_1_gt, comparator_2_gt, divider_1_out, divider_1_rem, divider_2_out,
       divider_2_rem, multiplier_1_cout, multiplier_1_out, multiplier_2_cout, multiplier_2_out, not_2_out,
       not_3_out, or_1_out, shifter_1_out, shifter_2_out, shifter_4_out, shifter_5_out, shifter_6_out,
       subtractor_1_bout, subtractor_1_out, undriven, xor_1_out;
  wire [7:3] pull_resistor_2_node, pull_resistor_3_node, pull_resistor_4_node, pull_resistor_5_node;
  wire [7:4] pull_resistor_6_node;
  wire [23:0] shifter_3_out, shifter_7_out;

  not not_1 (not_1_out, OutputEnable);
  Random random_1 ();  // open: clk, next, out, clr
  Clock clock_1 ();  // open: out
  Adder adder_1 (.a(A), .b(B), .out(adder_1_out), .cin(E[0]), .cout(adder_1_cout[0]));
  Subtractor subtractor_1 (.a(A), .b(B), .out(subtractor_1_out), .bin(E[0]), .bout(subtractor_1_bout[0]));
  Multiplier multiplier_1 (.a(A), .b(B), .out(multiplier_1_out), .cin(E), .cout(multiplier_1_cout));
  Divider divider_1 (.a(A), .b(B), .out(divider_1_out), .upper(E), .rem(divider_1_rem));
  Multiplier #(.mode("twosComplement")) multiplier_2 (
    .a(A), .b(B), .out(multiplier_2_out), .cin(E), .cout(multiplier_2_cout));
  Divider #(.mode("twosComplement")) divider_2 (.a(A), .b(B), .out(divider_2_out), .upper(E), .rem(divider_2_rem));
  BitFinder bitfinder_1 (.in(A), .found(bitfinder_1_found));  // open: index
  BitFinder bitfinder_2 (.in(A), .index(bitfinder_2_index), .found(bitfinder_2_found[0]));
  BitFinder #(.\type ("high1")) bitfinder_3 (.in(A), .index(bitfinder_3_index), .found(bitfinder_3_found[0]));
  BitFinder #(.\type ("low0")) bitfinder_4 (.in(A), .index(bitfinder_4_index), .found(bitfinder_4_found[0]));
  BitFinder #(.\type ("high0")) bitfinder_5 (.in(A), .index(bitfinder_5_index), .found(bitfinder_5_found[0]));
  Shifter #(.shift("rl")) shifter_1 (.in(A), .\dist (B[2:0]), .out(shifter_1_out));
  Shifter #(.shift("rr")) shifter_2 (.in(A), .\dist (B[2:0]), .out(shifter_2_out));
  Negator #(.width(3)) negator_1 (.in(B[2:0]), .out(negator_1_out));
  Shifter #(.shift("lr"), .width(24)) shifter_3 (.in({E, A, {8{1'b0}}}), .\dist ({2'b00, B[2:0]}), .out(shifter_3_out));
  Negator #(.width(3)) negator_2 (.in(B[2:0]), .out(negator_2_out));
  Shifter #(.shift("ar")) shifter_4 (.in(A), .\dist (B[2:0]), .out(shifter_4_out));
  BitAdder bitadder_1 (.in0(A), .out(bitadder_1_out));
  Comparator #(.mode("unsigned")) comparator_1 (
    .a(A), .b(B), .gt(comparator_1_gt[0]), .eq(comparator_1_gt[1]), .lt(comparator_1_gt[2]));
  Comparator comparator_2 (.a(A), .b(B), .gt(comparator_2_gt[0]), .eq(comparator_2_gt[1]), .lt(comparator_2_gt[2]));
  assign and_1_out = A & B;  // AND_Gate and_1, 8 bits wide
  assign or_1_out = A | B;  // OR_Gate or_1, 8 bits wide
  assign xor_1_out = A ^ B;  // XOR_Gate xor_1, 8 bits wide
  assign not_2_out = ~A;  // NOT_Gate not_2, 8 bits wide
  nor nor_1 (nor_1_out, M[5], M[6], M[7], not_1_out);
  not not_3 (not_3_out[0], bitfinder_1_found);
  Shifter shifter_5 (.in(E), .\dist (negator_1_out), .out(shifter_5_out));
  Shifter #(.shift("lr")) shifter_6 (.in(shifter_3_out[7:0]), .\dist (negator_2_out), .out(shifter_6_out));
  Shifter #(.width(24)) shifter_7 (.in({{8{1'b0}}, A, shifter_5_out}), .\dist ({2'b00, B[2:0]}), .out(shifter_7_out));
  Multiplexer #(.disabled("Z"), .select(5), .width(8)) multiplexer_1 (
    .in0(A), .in1(B), .in2(E), .in3(undriven), .in4(adder_1_out), .in5(subtractor_1_out),
    .in6(multiplier_1_out), .in7(divider_1_out), .in8(multiplier_2_out), .in9(divider_2_out),
    .in15(not_3_out), .in16({pull_resistor_2_node, bitfinder_2_index}),
    .in17({pull_resistor_3_node, bitfinder_3_index}), .in18({pull_resistor_4_node, bitfinder_4_index}),
    .in19({pull_resistor_5_node, bitfinder_5_index}), .in20(shifter_1_out), .in21(shifter_2_out),
    .in22(shifter_7_out[15:8]), .in23(shifter_3_out[15:8]), .in24(shifter_4_out),
    .in25({pull_resistor_6_node, bitadder_1_out}), .in26(comparator_1_gt), .in27(comparator_2_gt),
    .in28(and_1_out), .in29(or_1_out), .in30(xor_1_out), .in31(not_2_out), .out(R), .sel(M[4:0]),
    .en(nor_1_out));  // open: in10, in11, in12, in13, in14
  Pull_Resistor pull_resistor_1 (.node(not_3_out));
  Pull_Resistor pull_resistor_2 (.node({pull_resistor_2_node, bitfinder_2_index}));
  Pull_Resistor pull_resistor_3 (.node({pull_resistor_3_node, bitfinder_3_index}));
  Pull_Resistor pull_resistor_4 (.node({pull_resistor_4_node, bitfinder_4_index}));
  Pull_Resistor pull_resistor_5 (.node({pull_resistor_5_node, bitfinder_5_index}));
  Pull_Resistor pull_resistor_6 (.node({pull_resistor_6_node, bitadder_1_out}));
  Pull_Resistor pull_resistor_7 (.node(comparator_1_gt));
  Pull_Resistor pull_resistor_8 (.node(comparator_2_gt));
  Pull_Resistor pull_resistor_9 (.node(adder_1_cout));
  Pull_Resistor pull_resistor_10 (.node(subtractor_1_bout));
  Multiplexer #(.disabled("Z"), .select(5), .width(8)) multiplexer_2 (
    .in0(E), .in1(E), .in2(E), .in3(E), .in4(adder_1_cout), .in5(subtractor_1_bout), .in6(multiplier_1_cout),
    .in7(divider_1_rem), .in8(multiplier_2_cout), .in9(divider_2_rem), .in10(E), .in11(E), .in12(E),
    .in13(E), .in14(E), .in15(E), .in16(bitfinder_2_found), .in17(bitfinder_3_found),
    .in18(bitfinder_4_found), .in19(bitfinder_5_found), .in20(E), .in21(E), .in22(shifter_7_out[23:16]),
    .in23(shifter_6_out), .in24(E), .in25(E), .in26(E), .in27(E), .in28(E), .in29(E), .in30(E), .in31(E),
    .out(S), .sel(M[4:0]), .en(nor_1_out));
  Pull_Resistor pull_resistor_11 (.node(bitfinder_2_found));
  Pull_Resistor pull_resistor_12 (.node(bitfinder_3_found));
  Pull_Resistor pull_resistor_13 (.node(bitfinder_4_found));
  Pull_Resistor pull_resistor_14 (.node(bitfinder_5_found));
endmodule

module ALU3 (
  input  OutputEnable,
  input  [7:0] A,
  input  [7:0] B,
  input  [7:0] E,
  input  [7:0] M,
  output [7:0] R,
  output [7:0] S,
  output Carry
);

  wire decoder_1_out4, decoder_1_out5, decoder_1_out6, decoder_1_out7, decoder_1_out8, decoder_1_out9,
       decoder_1_out10, decoder_1_out16, decoder_1_out17, decoder_1_out18, decoder_1_out19, decoder_1_out22,
       decoder_1_out23, decoder_1_out27, not_1_out, not_2_out, or_2_out, or_3_out;
  wire [1:0] pull_resistor_3_node;
  wire [2:0] bit_extender_2_out, negator_1_out, negator_2_out, pull_resistor_4_node, xor_3_out;
  wire [3:0] bitadder_1_out;
  wire [7:0] adder_1_cout, adder_1_out, and_1_out, and_2_out, bcdaccelerator_1_r, bcdaccelerator_1_s,
       bit_extender_1_out, comparator_1_eq, controlled_buffer_1_out, controlled_buffer_2_out,
       divaccelerator_1_r, divaccelerator_1_s, multiplexer_1_out, multiplier_1_cout, multiplier_1_out,
       multiplier_2_cout, multiplier_2_out, not_3_out, or_4_out, shifter_1_out, shifter_2_out, shifter_4_out,
       shifter_5_out, shifter_6_out, shifter_7_out, shifter_7_out_2, shifter_7_out_3, subtractor_1_bout,
       subtractor_1_out, undriven, xor_1_out, xor_2_out;
  wire [7:3] pull_resistor_5_node;
  wire [7:4] pull_resistor_6_node;
  wire [23:0] shifter_3_out;

  or or_1 (Carry, decoder_1_out4, decoder_1_out5, decoder_1_out6, decoder_1_out7, decoder_1_out8, decoder_1_out9, decoder_1_out10, decoder_1_out22, decoder_1_out23, decoder_1_out27);
  Decoder #(.select(5)) decoder_1 (
    .out4(decoder_1_out4), .out5(decoder_1_out5), .out6(decoder_1_out6), .out7(decoder_1_out7),
    .out8(decoder_1_out8), .out9(decoder_1_out9), .out10(decoder_1_out10), .out16(decoder_1_out16),
    .out17(decoder_1_out17), .out18(decoder_1_out18), .out19(decoder_1_out19), .out22(decoder_1_out22),
    .out23(decoder_1_out23), .out27(decoder_1_out27), .sel(M[4:0]), .en(OutputEnable));  // open: out0, out1, out2, out3, out11, out12, out13, out14, out15, out20, out21, out24, out25, out26, out28, out29, out30, out31
  not not_1 (not_1_out, decoder_1_out5);
  assign controlled_buffer_1_out = not_1_out ? B : 8'bz;  // Controlled_Buffer controlled_buffer_1
  not not_2 (not_2_out, decoder_1_out7);
  assign controlled_buffer_2_out = not_2_out ? B : 8'bz;  // Controlled_Buffer controlled_buffer_2
  Random random_1 ();  // open: clk, next, out, clr
  Clock clock_1 ();  // open: out
  or or_2 (or_2_out, decoder_1_out5, E[0]);
  Adder adder_1 (.a(A), .b(controlled_buffer_1_out), .out(adder_1_out), .cin(or_2_out), .cout(adder_1_cout[0]));
  Pull_Resistor pull_resistor_1 (.node(controlled_buffer_1_out));
  or or_3 (or_3_out, decoder_1_out7, E[0]);
  Subtractor subtractor_1 (
    .a(A), .b(controlled_buffer_2_out), .out(subtractor_1_out), .bin(or_3_out), .bout(subtractor_1_bout[0]));
  Pull_Resistor pull_resistor_2 (.node(controlled_buffer_2_out));
  Multiplier multiplier_1 (.a(A), .b(B), .out(multiplier_1_out), .cin(E), .cout(multiplier_1_cout));
  Multiplier #(.mode("twosComplement")) multiplier_2 (
    .a(A), .b(B), .out(multiplier_2_out), .cin(E), .cout(multiplier_2_cout));
  Pull_Resistor pull_resistor_3 (.node(pull_resistor_3_node));
  Priority_Encoder #(.select(2)) priority_encoder_1 (
    .in0(decoder_1_out16), .in1(decoder_1_out17), .in2(decoder_1_out18), .in3(decoder_1_out19),
    .out(pull_resistor_3_node));  // open: gs, en_out, en_in
  Shifter #(.shift("rl")) shifter_1 (.in(A), .\dist (B[2:0]), .out(shifter_1_out));
  Shifter #(.shift("rr")) shifter_2 (.in(A), .\dist (B[2:0]), .out(shifter_2_out));
  Negator #(.width(3)) negator_1 (.in(B[2:0]), .out(negator_1_out));
  Shifter #(.shift("lr"), .width(24)) shifter_3 (.in({E, A, {8{1'b0}}}), .\dist ({2'b00, B[2:0]}), .out(shifter_3_out));
  Negator #(.width(3)) negator_2 (.in(B[2:0]), .out(negator_2_out));
  Shifter #(.shift("ar")) shifter_4 (.in(A), .\dist (B[2:0]), .out(shifter_4_out));
  BitAdder bitadder_1 (.in0(A), .out(bitadder_1_out));
  Comparator #(.mode("unsigned")) comparator_1 (
    .a(A), .b(B), .gt(comparator_1_eq[4]), .eq(comparator_1_eq[0]), .lt(comparator_1_eq[5]));
  Comparator comparator_2 (.a(A), .b(B), .gt(comparator_1_eq[6]), .lt(comparator_1_eq[7]));  // open: eq
  assign and_1_out = A & B;  // AND_Gate and_1, 8 bits wide
  assign or_4_out = A | B;  // OR_Gate or_4, 8 bits wide
  assign xor_1_out = A ^ B;  // XOR_Gate xor_1, 8 bits wide
  assign not_3_out = ~A;  // NOT_Gate not_3, 8 bits wide
  assign bit_extender_1_out = {{7{pull_resistor_3_node[1]}}, pull_resistor_3_node[1]};  // Bit_Extender bit_extender_1
  Multiplexer #(.enable("false"), .width(8)) multiplexer_1 (
    .in0(A), .in1({A[0], A[1], A[2], A[3], A[4], A[5], A[6], A[7]}), .out(multiplexer_1_out),
    .sel(pull_resistor_3_node[0]));
  Shifter shifter_5 (.in(E), .\dist (negator_1_out), .out(shifter_5_out));
  Shifter #(.shift("lr")) shifter_6 (.in(shifter_3_out[7:0]), .\dist (negator_2_out), .out(shifter_6_out));
  DIVaccelerator divaccelerator_1 (.A(A), .B(B), .E(E), .R(divaccelerator_1_r), .S(divaccelerator_1_s));
  assign xor_2_out = bit_extender_1_out ^ multiplexer_1_out;  // XOR_Gate xor_2, 8 bits wide
  Shifter #(.width(24)) shifter_7 (
    .in({{8{1'b0}}, A, shifter_5_out}), .\dist ({2'b00, B[2:0]}),
    .out({shifter_7_out_3, shifter_7_out_2, shifter_7_out}));
  BCDaccelerator bcdaccelerator_1 (.A(A), .B(B), .E(E), .R(bcdaccelerator_1_r), .S(bcdaccelerator_1_s));
  assign bit_extender_2_out = {{2{pull_resistor_3_node[0]}}, pull_resistor_3_node[0]};  // Bit_Extender bit_extender_2
  Pull_Resistor pull_resistor_4 (.node(pull_resistor_4_node));
  Priority_Encoder priority_encoder_2 (
    .in0(xor_2_out[0]), .in1(xor_2_out[1]), .in2(xor_2_out[2]), .in3(xor_2_out[3]), .in4(xor_2_out[4]),
    .in5(xor_2_out[5]), .in6(xor_2_out[6]), .in7(xor_2_out[7]), .out(pull_resistor_4_node),
    .gs(comparator_1_eq[2]), .en_out(comparator_1_eq[1]));  // open: en_in
  assign xor_3_out = bit_extender_2_out ^ pull_resistor_4_node;  // XOR_Gate xor_3, 3 bits wide
  assign and_2_out = {comparator_1_eq[7:4], 1'b0, comparator_1_eq[2:0]} & E;  // AND_Gate and_2, 8 bits wide
  Multiplexer #(.disabled("Z"), .select(5), .width(8)) multiplexer_2 (
    .in0(A), .in1(B), .in2(E), .in3(undriven), .in4(adder_1_out), .in5(adder_1_out), .in6(subtractor_1_out),
    .in7(subtractor_1_out), .in8(multiplier_1_out), .in9(multiplier_2_out), .in10(divaccelerator_1_r),
    .in16({pull_resistor_5_node, xor_3_out}), .in17({pull_resistor_5_node, xor_3_out}),
    .in18({pull_resistor_5_node, xor_3_out}), .in19({pull_resistor_5_node, xor_3_out}), .in20(shifter_1_out),
    .in21(shifter_2_out), .in22(shifter_7_out_2), .in23(shifter_3_out[15:8]), .in24(shifter_4_out),
    .in25({pull_resistor_6_node, bitadder_1_out}), .in26(and_2_out), .in27(bcdaccelerator_1_r),
    .in28(and_1_out), .in29(or_4_out), .in30(xor_1_out), .in31(not_3_out), .out(R), .sel(M[4:0]),
    .en(OutputEnable));  // open: in11, in12, in13, in14, in15
  Pull_Resistor pull_resistor_5 (.node({pull_resistor_5_node, xor_3_out}));
  Pull_Resistor pull_resistor_6 (.node({pull_resistor_6_node, bitadder_1_out}));
  Pull_Resistor pull_resistor_7 (.node(and_2_out));
  Pull_Resistor pull_resistor_8 (.node(adder_1_cout));
  Pull_Resistor pull_resistor_9 (.node(subtractor_1_bout));
  Multiplexer #(.disabled("Z"), .select(5), .width(8)) multiplexer_3 (
    .in0(E), .in1(E), .in2(E), .in3(E), .in4(adder_1_cout), .in5(adder_1_cout), .in6(subtractor_1_bout),
    .in7(subtractor_1_bout), .in8(multiplier_1_cout), .in9(multiplier_2_cout), .in10(divaccelerator_1_s),
    .in11(E), .in12(E), .in13(E), .in14(E), .in15(E), .in16(E), .in17(E), .in18(E), .in19(E), .in20(E),
    .in21(E), .in22(shifter_7_out_3), .in23(shifter_6_out), .in24(E), .in25(E), .in26(E),
    .in27(bcdaccelerator_1_s), .in28(E), .in29(E), .in30(E), .in31(E), .out(S), .sel(M[4:0]),
    .en(OutputEnable));
endmodule

module BCDaccelerator (
  input  [7:0] A,
  input  [7:0] B,
  input  [7:0] E,
  output [7:0] R,
  output [7:0] S
);

  wire comparator_1_gt, comparator_2_gt;
  wire [3:0] controlled_buffer_1_out, controlled_buffer_2_out;

  // Probe on B
  Comparator #(.mode("unsigned"), .width(4)) comparator_1 (
    .a(A[3:0]), .b(B[7:4]), .gt(comparator_1_gt));  // open: eq, lt
  Comparator #(.mode("unsigned"), .width(4)) comparator_2 (
    .a(A[7:4]), .b(B[7:4]), .gt(comparator_2_gt));  // open: eq, lt
  assign controlled_buffer_1_out = comparator_1_gt ? B[3:0] : 4'bz;  // Controlled_Buffer controlled_buffer_1
  assign controlled_buffer_2_out = comparator_2_gt ? B[3:0] : 4'bz;  // Controlled_Buffer controlled_buffer_2
  Pull_Resistor pull_resistor_1 (.node({controlled_buffer_2_out, controlled_buffer_1_out}));
  Adder adder_1 (
    .a({controlled_buffer_2_out, controlled_buffer_1_out}), .b(A), .out({S[0], R[7:1]}));  // open: cin, cout
  Pull_Resistor pull_resistor_2 (.node(S));

  assign R[0] = E[0];
endmodule

module DIVaccelerator (
  input  [7:0] A,
  input  [7:0] B,
  input  [7:0] E,
  output [7:0] R,
  output [7:0] S
);

  wire subtractor_1_bout;
  wire [7:0] subtractor_1_out;
  wire [7:7] multiplexer_1_out;

  Subtractor subtractor_1 (.a(E), .b(B), .out(subtractor_1_out), .bout(subtractor_1_bout));  // open: bin
  not not_1 (R[0], subtractor_1_bout);
  Multiplexer #(.enable("false"), .width(8)) multiplexer_1 (
    .in0(subtractor_1_out), .in1(E), .out({multiplexer_1_out[7], S[7:1]}), .sel(subtractor_1_bout));

  assign R[7:1] = A[6:0];
  assign S[0] = A[7];
endmodule

module Cache (
  input  [47:0] in_1,
  input  in_2
);

  wire and_1_out, clock_1_out, comparator_1_eq, comparator_2_eq, comparator_3_eq, comparator_4_eq,
       comparator_5_eq, comparator_6_eq, comparator_7_eq, comparator_8_eq, comparator_9_eq, comparator_10_eq,
       comparator_11_eq, comparator_12_eq, comparator_13_eq, comparator_14_eq, comparator_15_eq,
       comparator_16_eq, comparator_17_eq, decoder_1_out0, decoder_1_out1, decoder_1_out2, decoder_1_out3,
       decoder_1_out4, decoder_1_out5, decoder_1_out6, decoder_1_out7, decoder_1_out8, decoder_1_out9,
       decoder_1_out10, decoder_1_out11, decoder_1_out12, decoder_1_out13, decoder_1_out14, decoder_1_out15,
       not_1_out, not_2_out, not_3_out, undriven, undriven_2;
  wire [1:0] counter_1_q;
  wire [3:0] multiplexer_1_out, multiplexer_2_out, multiplexer_3_out, multiplexer_4_out, multiplexer_5_out,
       Newer_dout, Newest_q, Older_dout, Oldest_q, priority_encoder_1_out;
  wire [47:0] register_1_q, register_2_q, register_3_q, register_4_q, register_5_q, register_6_q,
       register_7_q, register_8_q, register_9_q, register_10_q, register_11_q, register_12_q, register_13_q,
       register_14_q, register_15_q, register_16_q, register_17_q;

  Decoder #(.select(4)) decoder_1 (
    .out0(decoder_1_out0), .out1(decoder_1_out1), .out2(decoder_1_out2), .out3(decoder_1_out3),
    .out4(decoder_1_out4), .out5(decoder_1_out5), .out6(decoder_1_out6), .out7(decoder_1_out7),
    .out8(decoder_1_out8), .out9(decoder_1_out9), .out10(decoder_1_out10), .out11(decoder_1_out11),
    .out12(decoder_1_out12), .out13(decoder_1_out13), .out14(decoder_1_out14), .out15(decoder_1_out15),
    .sel(multiplexer_1_out), .en(undriven));
  Register #(.width(48)) register_1 (.D(in_1), .en(in_2), .clk(counter_1_q[0]), .Q(register_1_q));  // open: clr
  Register #(.width(48)) register_2 (
    .D(register_1_q), .en(decoder_1_out0), .clk(not_2_out), .Q(register_2_q));  // open: clr
  Register #(.width(48)) register_3 (
    .D(register_1_q), .en(decoder_1_out1), .clk(not_2_out), .Q(register_3_q));  // open: clr
  Register #(.width(48)) register_4 (
    .D(register_1_q), .en(decoder_1_out2), .clk(not_2_out), .Q(register_4_q));  // open: clr
  Register #(.width(48)) register_5 (
    .D(register_1_q), .en(decoder_1_out3), .clk(not_2_out), .Q(register_5_q));  // open: clr
  Register #(.width(48)) register_6 (
    .D(register_1_q), .en(decoder_1_out4), .clk(not_2_out), .Q(register_6_q));  // open: clr
  Register #(.width(48)) register_7 (
    .D(register_1_q), .en(decoder_1_out5), .clk(not_2_out), .Q(register_7_q));  // open: clr
  Register #(.width(48)) register_8 (
    .D(register_1_q), .en(decoder_1_out6), .clk(not_2_out), .Q(register_8_q));  // open: clr
  Register #(.width(48)) register_9 (
    .D(register_1_q), .en(decoder_1_out7), .clk(not_2_out), .Q(register_9_q));  // open: clr
  Register #(.width(48)) register_10 (
    .D(register_1_q), .en(decoder_1_out8), .clk(not_2_out), .Q(register_10_q));  // open: clr
  Register #(.width(48)) register_11 (
    .D(register_1_q), .en(decoder_1_out9), .clk(not_2_out), .Q(register_11_q));  // open: clr
  Register #(.width(48)) register_12 (
    .D(register_1_q), .en(decoder_1_out10), .clk(not_2_out), .Q(register_12_q));  // open: clr
  Register #(.width(48)) register_13 (
    .D(register_1_q), .en(decoder_1_out11), .clk(not_2_out), .Q(register_13_q));  // open: clr
  Register #(.width(48)) register_14 (
    .D(register_1_q), .en(decoder_1_out12), .clk(not_2_out), .Q(register_14_q));  // open: clr
  Register #(.width(48)) register_15 (
    .D(register_1_q), .en(decoder_1_out13), .clk(not_2_out), .Q(register_15_q));  // open: clr
  Register #(.width(48)) register_16 (
    .D(register_1_q), .en(decoder_1_out14), .clk(not_2_out), .Q(register_16_q));  // open: clr
  Register #(.width(48)) register_17 (
    .D(register_1_q), .en(decoder_1_out15), .clk(not_2_out), .Q(register_17_q));  // open: clr
  Comparator #(.width(48)) comparator_1 (.a(register_1_q), .b(register_2_q), .eq(comparator_1_eq));  // open: gt, lt
  Comparator #(.width(48)) comparator_2 (.a(register_1_q), .b(register_3_q), .eq(comparator_2_eq));  // open: gt, lt
  Comparator #(.width(48)) comparator_3 (.a(register_1_q), .b(register_4_q), .eq(comparator_3_eq));  // open: gt, lt
  Comparator #(.width(48)) comparator_4 (.a(register_1_q), .b(register_5_q), .eq(comparator_4_eq));  // open: gt, lt
  Comparator #(.width(48)) comparator_5 (.a(register_1_q), .b(register_6_q), .eq(comparator_5_eq));  // open: gt, lt
  Comparator #(.width(48)) comparator_6 (.a(register_1_q), .b(register_7_q), .eq(comparator_6_eq));  // open: gt, lt
  Comparator #(.width(48)) comparator_7 (.a(register_1_q), .b(register_8_q), .eq(comparator_7_eq));  // open: gt, lt
  Comparator #(.width(48)) comparator_8 (.a(register_1_q), .b(register_9_q), .eq(comparator_8_eq));  // open: gt, lt
  Comparator #(.width(48)) comparator_9 (.a(register_1_q), .b(register_10_q), .eq(comparator_9_eq));  // open: gt, lt
  Comparator #(.width(48)) comparator_10 (.a(register_1_q), .b(register_11_q), .eq(comparator_10_eq));  // open: gt, lt
  Comparator #(.width(48)) comparator_11 (.a(register_1_q), .b(register_12_q), .eq(comparator_11_eq));  // open: gt, lt
  Comparator #(.width(48)) comparator_12 (.a(register_1_q), .b(register_13_q), .eq(comparator_12_eq));  // open: gt, lt
  Comparator #(.width(48)) comparator_13 (.a(register_1_q), .b(register_14_q), .eq(comparator_13_eq));  // open: gt, lt
  Comparator #(.width(48)) comparator_14 (.a(register_1_q), .b(register_15_q), .eq(comparator_14_eq));  // open: gt, lt
  Comparator #(.width(48)) comparator_15 (.a(register_1_q), .b(register_16_q), .eq(comparator_15_eq));  // open: gt, lt
  Comparator #(.width(48)) comparator_16 (.a(register_1_q), .b(register_17_q), .eq(comparator_16_eq));  // open: gt, lt
  Priority_Encoder #(.select(4)) priority_encoder_1 (
    .in0(comparator_1_eq), .in1(comparator_2_eq), .in2(comparator_3_eq), .in3(comparator_4_eq),
    .in4(comparator_5_eq), .in5(comparator_6_eq), .in6(comparator_7_eq), .in7(comparator_8_eq),
    .in8(comparator_9_eq), .in9(comparator_10_eq), .in10(comparator_11_eq), .in11(comparator_12_eq),
    .in12(comparator_13_eq), .in13(comparator_14_eq), .in14(comparator_15_eq), .in15(comparator_16_eq),
    .out(priority_encoder_1_out));
  Counter #(.max('h3), .width(2)) counter_1 (.Q(counter_1_q), .clk(not_1_out));  // open: load, D, count, carry, up, clr
  not not_1 (not_1_out, clock_1_out);
  Clock clock_1 (.out(clock_1_out));
  not not_2 (not_2_out, counter_1_q[0]);
  Register #(.width(4)) Oldest (.D(Newer_dout), .en(and_1_out), .clk(clock_1_out), .Q(Oldest_q));  // open: clr
  Register #(.width(4)) Newest (.D(multiplexer_1_out), .en(not_3_out), .clk(clock_1_out), .Q(Newest_q));  // open: clr
  Multiplexer #(.enable("false"), .width(4)) multiplexer_1 (
    .in0(priority_encoder_1_out), .in1(Oldest_q), .out(multiplexer_1_out), .sel(undriven_2));
  Multiplexer #(.enable("false"), .width(4)) multiplexer_2 (
    .in0(Oldest_q), .in1(Newer_dout), .out(multiplexer_2_out), .sel(counter_1_q[0]));
  Multiplexer #(.enable("false"), .width(4)) multiplexer_3 (
    .in0(Newest_q), .in1(Newer_dout), .out(multiplexer_3_out), .sel(counter_1_q[0]));
  // Probe on {Older_dout, Newer_dout}
  Comparator #(.width(4)) comparator_17 (.a(Older_dout), .b(Newest_q), .eq(comparator_17_eq));  // open: gt, lt
  and and_1 (and_1_out, comparator_17_eq, counter_1_q[0]);
  Multiplexer #(.enable("false"), .width(4)) multiplexer_4 (
    .in0(multiplexer_1_out), .in1(Older_dout), .out(multiplexer_4_out), .sel(counter_1_q[0]));
  Multiplexer #(.enable("false"), .width(4)) multiplexer_5 (
    .in0(multiplexer_1_out), .in1(Newer_dout), .out(multiplexer_5_out), .sel(counter_1_q[0]));
  not not_3 (not_3_out, counter_1_q[0]);
  RAM #(.addrWidth(4), .dataWidth(4), .readbehav("war")) Newer (
    .addr(multiplexer_4_out), .we(1'b1), .oe(1'b1), .clk(clock_1_out), .din(multiplexer_2_out),
    .dout(Newer_dout));
  RAM #(.addrWidth(4), .dataWidth(4), .readbehav("war")) Older (
    .addr(multiplexer_5_out), .we(1'b1), .oe(1'b1), .clk(clock_1_out), .din(multiplexer_3_out),
    .dout(Older_dout));
  RAM #(.addrWidth(4), .dataWidth(64)) ram_1 (.addr(multiplexer_1_out));  // open: we, oe, clk, din, dout
endmodule

module CacheRegister (
  input  [63:0] in_1,
  input  in_2,
  input  [3:0] in_3
);

  wire and_1_out, and_2_out, clock_1_out, clock_2_out, clock_3_out, clock_4_out, comparator_1_eq,
       comparator_2_eq, comparator_3_eq, comparator_4_eq, comparator_5_eq, comparator_6_eq, comparator_7_eq,
       comparator_8_eq, comparator_9_eq, comparator_10_eq, comparator_11_eq, comparator_12_eq,
       comparator_13_eq, comparator_14_eq, comparator_15_eq, comparator_16_eq, comparator_17_eq,
       comparator_18_eq, decoder_1_out0, decoder_1_out1, decoder_1_out2, decoder_1_out3, decoder_1_out4,
       decoder_1_out5, decoder_1_out6, decoder_1_out7, decoder_1_out8, decoder_1_out9, decoder_1_out10,
       decoder_1_out11, decoder_1_out12, decoder_1_out13, decoder_1_out14, decoder_1_out15, not_1_out,
       not_2_out, not_3_out, t_ff_1_q, undriven_2, undriven_7;
  wire [1:0] counter_2_q;
  wire [3:0] adder_1_out, adder_2_out, multiplexer_1_out, multiplexer_2_out, multiplexer_3_out,
       multiplexer_4_out, multiplexer_5_out, multiplexer_6_out, multiplexer_7_out, multiplexer_8_out,
       multiplexer_9_out, Nesest_dout, Newer_dout, Older_dout, Oldest_dout, priority_encoder_1_out,
       pull_resistor_2_node, pull_resistor_3_node, register_2_q, register_3_q, undriven, undriven_3,
       undriven_4, undriven_5, undriven_6, undriven_8, undriven_9, undriven_10;
  wire [7:0] counter_1_q;
  wire [7:4] register_1_q_2;
  wire [59:0] ram_1_dout, ram_2_dout, ram_3_dout, ram_4_dout, ram_5_dout, ram_6_dout, ram_7_dout, ram_8_dout,
       ram_9_dout, ram_10_dout, ram_11_dout, ram_12_dout, ram_13_dout, ram_14_dout, ram_15_dout, ram_16_dout;
  wire [63:4] register_1_q;

  Decoder #(.select(4)) decoder_1 (
    .out0(decoder_1_out0), .out1(decoder_1_out1), .out2(decoder_1_out2), .out3(decoder_1_out3),
    .out4(decoder_1_out4), .out5(decoder_1_out5), .out6(decoder_1_out6), .out7(decoder_1_out7),
    .out8(decoder_1_out8), .out9(decoder_1_out9), .out10(decoder_1_out10), .out11(decoder_1_out11),
    .out12(decoder_1_out12), .out13(decoder_1_out13), .out14(decoder_1_out14), .out15(decoder_1_out15),
    .sel(undriven));  // open: en
  Clock clock_1 (.out(clock_1_out));
  Register #(.width(64)) register_1 (
    .D(in_1), .en(in_2), .clk(undriven_2), .Q({register_1_q, register_1_q_2}));  // open: clr
  RAM #(.addrWidth(4), .dataWidth(60), .enables("line")) ram_1 (
    .addr(register_1_q_2), .we(decoder_1_out0), .clk(clock_1_out), .din(register_1_q), .dout(ram_1_dout));
  RAM #(.addrWidth(4), .dataWidth(60), .enables("line")) ram_2 (
    .addr(register_1_q_2), .we(decoder_1_out1), .clk(clock_1_out), .din(register_1_q), .dout(ram_2_dout));
  RAM #(.addrWidth(4), .dataWidth(60), .enables("line")) ram_3 (
    .addr(register_1_q_2), .we(decoder_1_out2), .clk(clock_1_out), .din(register_1_q), .dout(ram_3_dout));
  RAM #(.addrWidth(4), .dataWidth(60), .enables("line")) ram_4 (
    .addr(register_1_q_2), .we(decoder_1_out3), .clk(clock_1_out), .din(register_1_q), .dout(ram_4_dout));
  RAM #(.addrWidth(4), .dataWidth(60), .enables("line")) ram_5 (
    .addr(register_1_q_2), .we(decoder_1_out4), .clk(clock_1_out), .din(register_1_q), .dout(ram_5_dout));
  RAM #(.addrWidth(4), .dataWidth(60), .enables("line")) ram_6 (
    .addr(register_1_q_2), .we(decoder_1_out5), .clk(clock_1_out), .din(register_1_q), .dout(ram_6_dout));
  RAM #(.addrWidth(4), .dataWidth(60), .enables("line")) ram_7 (
    .addr(register_1_q_2), .we(decoder_1_out6), .clk(clock_1_out), .din(register_1_q), .dout(ram_7_dout));
  RAM #(.addrWidth(4), .dataWidth(60), .enables("line")) ram_8 (
    .addr(register_1_q_2), .we(decoder_1_out7), .clk(clock_1_out), .din(register_1_q), .dout(ram_8_dout));
  RAM #(.addrWidth(4), .dataWidth(60), .enables("line")) ram_9 (
    .addr(register_1_q_2), .we(decoder_1_out8), .clk(clock_1_out), .din(register_1_q), .dout(ram_9_dout));
  RAM #(.addrWidth(4), .dataWidth(60), .enables("line")) ram_10 (
    .addr(register_1_q_2), .we(decoder_1_out9), .clk(clock_1_out), .din(register_1_q), .dout(ram_10_dout));
  RAM #(.addrWidth(4), .dataWidth(60), .enables("line")) ram_11 (
    .addr(register_1_q_2), .we(decoder_1_out10), .clk(clock_1_out), .din(register_1_q), .dout(ram_11_dout));
  RAM #(.addrWidth(4), .dataWidth(60), .enables("line")) ram_12 (
    .addr(register_1_q_2), .we(decoder_1_out11), .clk(clock_1_out), .din(register_1_q), .dout(ram_12_dout));
  RAM #(.addrWidth(4), .dataWidth(60), .enables("line")) ram_13 (
    .addr(register_1_q_2), .we(decoder_1_out12), .clk(clock_1_out), .din(register_1_q), .dout(ram_13_dout));
  RAM #(.addrWidth(4), .dataWidth(60), .enables("line")) ram_14 (
    .addr(register_1_q_2), .we(decoder_1_out13), .clk(clock_1_out), .din(register_1_q), .dout(ram_14_dout));
  RAM #(.addrWidth(4), .dataWidth(60), .enables("line")) ram_15 (
    .addr(register_1_q_2), .we(decoder_1_out14), .clk(clock_1_out), .din(register_1_q), .dout(ram_15_dout));
  RAM #(.addrWidth(4), .dataWidth(60), .enables("line")) ram_16 (
    .addr(register_1_q_2), .we(decoder_1_out15), .clk(clock_1_out), .din(register_1_q), .dout(ram_16_dout));
  Comparator #(.width(60)) comparator_1 (.a(ram_1_dout), .b(register_1_q), .eq(comparator_1_eq));  // open: gt, lt
  Comparator #(.width(60)) comparator_2 (.a(ram_2_dout), .b(register_1_q), .eq(comparator_2_eq));  // open: gt, lt
  Comparator #(.width(60)) comparator_3 (.a(ram_3_dout), .b(register_1_q), .eq(comparator_3_eq));  // open: gt, lt
  Comparator #(.width(60)) comparator_4 (.a(ram_4_dout), .b(register_1_q), .eq(comparator_4_eq));  // open: gt, lt
  Comparator #(.width(60)) comparator_5 (.a(ram_5_dout), .b(register_1_q), .eq(comparator_5_eq));  // open: gt, lt
  Comparator #(.width(60)) comparator_6 (.a(ram_6_dout), .b(register_1_q), .eq(comparator_6_eq));  // open: gt, lt
  Comparator #(.width(60)) comparator_7 (.a(ram_7_dout), .b(register_1_q), .eq(comparator_7_eq));  // open: gt, lt
  Comparator #(.width(60)) comparator_8 (.a(ram_8_dout), .b(register_1_q), .eq(comparator_8_eq));  // open: gt, lt
  Comparator #(.width(60)) comparator_9 (.a(ram_9_dout), .b(register_1_q), .eq(comparator_9_eq));  // open: gt, lt
  Comparator #(.width(60)) comparator_10 (.a(ram_10_dout), .b(register_1_q), .eq(comparator_10_eq));  // open: gt, lt
  Comparator #(.width(60)) comparator_11 (.a(ram_11_dout), .b(register_1_q), .eq(comparator_11_eq));  // open: gt, lt
  Comparator #(.width(60)) comparator_12 (.a(ram_12_dout), .b(register_1_q), .eq(comparator_12_eq));  // open: gt, lt
  Comparator #(.width(60)) comparator_13 (.a(ram_13_dout), .b(register_1_q), .eq(comparator_13_eq));  // open: gt, lt
  Comparator #(.width(60)) comparator_14 (.a(ram_14_dout), .b(register_1_q), .eq(comparator_14_eq));  // open: gt, lt
  Comparator #(.width(60)) comparator_15 (.a(ram_15_dout), .b(register_1_q), .eq(comparator_15_eq));  // open: gt, lt
  Comparator #(.width(60)) comparator_16 (.a(ram_16_dout), .b(register_1_q), .eq(comparator_16_eq));  // open: gt, lt
  Priority_Encoder #(.select(4)) priority_encoder_1 (
    .in0(comparator_1_eq), .in1(comparator_2_eq), .in2(comparator_3_eq), .in3(comparator_4_eq),
    .in4(comparator_5_eq), .in5(comparator_6_eq), .in6(comparator_7_eq), .in7(comparator_8_eq),
    .in8(comparator_9_eq), .in9(comparator_10_eq), .in10(comparator_11_eq), .in11(comparator_12_eq),
    .in12(comparator_13_eq), .in13(comparator_14_eq), .in14(comparator_15_eq), .in15(comparator_16_eq),
    .out(priority_encoder_1_out));
  T_Flip_Flop #(.trigger("falling")) t_ff_1 (.T(1'b1), .clk(clock_2_out), .Q(t_ff_1_q));  // open: Qn, reset, preset
  Clock clock_2 (.out(clock_2_out));
  Comparator #(.width(4)) comparator_17 (.a(Oldest_dout), .b(in_3), .eq(comparator_17_eq));  // open: gt, lt
  RAM #(.addrWidth(4), .dataWidth(4), .enables("line")) Oldest (
    .addr(register_1_q_2), .we(and_1_out), .clk(clock_2_out), .din(register_3_q), .dout(Oldest_dout));
  and and_1 (and_1_out, t_ff_1_q, comparator_17_eq);
  RAM #(.addrWidth(4), .dataWidth(4), .enables("line")) Nesest (
    .addr(register_1_q_2), .we(t_ff_1_q), .clk(clock_2_out), .din(in_3), .dout(Nesest_dout));
  Clock clock_3 (.out(clock_3_out));
  Counter counter_1 (.Q(counter_1_q), .clk(clock_3_out));  // open: load, D, count, carry, up, clr
  Multiplexer #(.enable("false"), .width(4)) multiplexer_1 (
    .in0(in_3), .in1(register_3_q), .out(multiplexer_1_out), .sel(t_ff_1_q));
  Multiplexer #(.enable("false"), .width(4)) multiplexer_2 (
    .in0(Oldest_dout), .in1(register_2_q), .out(multiplexer_2_out), .sel(t_ff_1_q));
  Multiplexer #(.enable("false"), .width(4)) multiplexer_3 (
    .in0(in_3), .in1(register_2_q), .out(multiplexer_3_out), .sel(t_ff_1_q));
  Multiplexer #(.enable("false"), .width(4)) multiplexer_4 (
    .in0(Nesest_dout), .in1(register_3_q), .out(multiplexer_4_out), .sel(t_ff_1_q));
  Pull_Resistor pull_resistor_1 (.node(t_ff_1_q));
  Pull_Resistor pull_resistor_2 (.node(pull_resistor_2_node));
  // Probe on adder_1_out
  Adder #(.width(4)) adder_1 (
    .a(pull_resistor_2_node), .b(counter_1_q[3:0]), .out(adder_1_out), .cin(1'b1));  // open: cout
  // Probe on adder_2_out
  Adder #(.width(4)) adder_2 (.a(counter_1_q[3:0]), .b(pull_resistor_3_node), .out(adder_2_out));  // open: cin, cout
  Pull_Resistor #(.pull(1)) pull_resistor_3 (.node(pull_resistor_3_node));
  RAM #(.dataWidth(4), .enables("line")) Newer (
    .addr({register_1_q_2, multiplexer_1_out}), .we(1'b1), .clk(clock_2_out), .din(undriven_3),
    .dout(Newer_dout));
  RAM #(.dataWidth(4), .enables("line")) Older (
    .addr({register_1_q_2, multiplexer_3_out}), .we(1'b1), .clk(clock_2_out), .din(undriven_4),
    .dout(Older_dout));
  // Probe on Newer_dout
  Register #(.width(4)) register_2 (.D(Newer_dout), .en(1'b1), .clk(clock_2_out), .Q(register_2_q));  // open: clr
  // Probe on Older_dout
  Register #(.width(4)) register_3 (.D(Older_dout), .en(1'b1), .clk(clock_2_out), .Q(register_3_q));  // open: clr
  not not_1 (not_1_out, clock_4_out);
  Counter #(.max('h3), .width(2)) counter_2 (.Q(counter_2_q), .clk(not_1_out));  // open: load, D, count, carry, up, clr
  Clock clock_4 (.out(clock_4_out));
  not not_2 (not_2_out, counter_2_q[0]);
  Multiplexer #(.enable("false"), .width(4)) multiplexer_5 (
    .in0(undriven_5), .in1(undriven_6), .out(multiplexer_5_out), .sel(undriven_7));
  Multiplexer #(.enable("false"), .width(4)) multiplexer_6 (
    .in0(undriven_6), .in1(undriven_9), .out(multiplexer_6_out), .sel(counter_2_q[0]));
  Comparator #(.width(4)) comparator_18 (.a(undriven_10), .b(undriven_8), .eq(comparator_18_eq));  // open: gt, lt
  Multiplexer #(.enable("false"), .width(4)) multiplexer_7 (
    .in0(undriven_8), .in1(undriven_9), .out(multiplexer_7_out), .sel(counter_2_q[0]));
  // Probe on {undriven_10, undriven_9}
  Multiplexer #(.enable("false"), .width(4)) multiplexer_8 (
    .in0(multiplexer_5_out), .in1(undriven_10), .out(multiplexer_8_out), .sel(counter_2_q[0]));
  Multiplexer #(.enable("false"), .width(4)) multiplexer_9 (
    .in0(multiplexer_5_out), .in1(undriven_9), .out(multiplexer_9_out), .sel(counter_2_q[0]));
  and and_2 (and_2_out, comparator_18_eq, counter_2_q[0]);
  not not_3 (not_3_out, counter_2_q[0]);
  RAM #(.addrWidth(4), .dataWidth(64)) ram_17 (.addr(multiplexer_5_out));  // open: we, oe, clk, din, dout
endmodule

module cacheLogic (
  input  [7:0] Data,
  input  [15:0] Address,
  input  Write,
  input  Enable
);

  wire and_1_out, clock_1_out, comparator_1_eq, comparator_2_eq, decoder_1_out0, not_1_out, not_2_out,
       priority_encoder_1_en_out;
  wire [1:0] counter_1_q;
  wire [3:0] multiplexer_1_out, multiplexer_2_out, multiplexer_3_out, multiplexer_4_out, multiplexer_5_out,
       Newer_dout, Newest_q, Older_dout, Oldest_q, priority_encoder_1_out;
  wire [15:0] register_1_q;

  Decoder #(.select(4)) decoder_1 (
    .out0(decoder_1_out0), .sel(multiplexer_1_out), .en(priority_encoder_1_en_out));  // open: out1, out2, out3, out4, out5, out6, out7, out8, out9, out10, out11, out12, out13, out14, out15
  // Probe on nothing
  Register #(.width(16)) register_1 (.D(Address), .en(decoder_1_out0), .Q(register_1_q));  // open: clk, clr
  Comparator #(.width(16)) comparator_1 (.a(register_1_q), .b(Address), .eq(comparator_1_eq));  // open: gt, lt
  Priority_Encoder #(.select(4)) priority_encoder_1 (
    .in0(comparator_1_eq), .out(priority_encoder_1_out), .en_out(priority_encoder_1_en_out));  // open: in1, in2, in3, in4, in5, in6, in7, in8, in9, in10, in11, in12, in13, in14, in15, gs, en_in
  Counter #(.max('h3), .width(2)) counter_1 (.Q(counter_1_q), .clk(not_1_out));  // open: load, D, count, carry, up, clr
  not not_1 (not_1_out, clock_1_out);
  Clock clock_1 (.out(clock_1_out));
  Register #(.width(4)) Oldest (.D(Newer_dout), .en(and_1_out), .clk(clock_1_out), .Q(Oldest_q));  // open: clr
  Register #(.width(4)) Newest (.D(multiplexer_1_out), .en(not_2_out), .clk(clock_1_out), .Q(Newest_q));  // open: clr
  Multiplexer #(.enable("false"), .width(4)) multiplexer_1 (
    .in0(priority_encoder_1_out), .in1(Oldest_q), .out(multiplexer_1_out), .sel(priority_encoder_1_en_out));
  Multiplexer #(.enable("false"), .width(4)) multiplexer_2 (
    .in0(Oldest_q), .in1(Newer_dout), .out(multiplexer_2_out), .sel(counter_1_q[0]));
  Comparator #(.width(4)) comparator_2 (.a(Older_dout), .b(Newest_q), .eq(comparator_2_eq));  // open: gt, lt
  Multiplexer #(.enable("false"), .width(4)) multiplexer_3 (
    .in0(Newest_q), .in1(Newer_dout), .out(multiplexer_3_out), .sel(counter_1_q[0]));
  // Probe on {Older_dout, Newer_dout}
  Multiplexer #(.enable("false"), .width(4)) multiplexer_4 (
    .in0(multiplexer_1_out), .in1(Older_dout), .out(multiplexer_4_out), .sel(counter_1_q[0]));
  Multiplexer #(.enable("false"), .width(4)) multiplexer_5 (
    .in0(multiplexer_1_out), .in1(Newer_dout), .out(multiplexer_5_out), .sel(counter_1_q[0]));
  and and_1 (and_1_out, comparator_2_eq, counter_1_q[0]);
  RAM #(.addrWidth(4), .databus("bidir")) ram_1 (.addr(multiplexer_1_out), .data(Data));  // open: we, oe, clk
  not not_2 (not_2_out, counter_1_q[0]);
  RAM #(.addrWidth(4), .dataWidth(4), .readbehav("war")) Newer (
    .addr(multiplexer_4_out), .we(1'b1), .oe(1'b1), .clk(clock_1_out), .din(multiplexer_2_out),
    .dout(Newer_dout));
  RAM #(.addrWidth(4), .dataWidth(4), .readbehav("war")) Older (
    .addr(multiplexer_5_out), .we(1'b1), .oe(1'b1), .clk(clock_1_out), .din(multiplexer_3_out),
    .dout(Older_dout));
endmodule
